# Fritzing sketch Morpheus_ElectronicScheme (saved by Fritzing 1.0.1rc)

parts:
  RPI_4 = Raspberry Pi 4B
  Adafruit_Speaker_Bonnet = Adafruit Stereo 3W Speaker Bonnet [part_number="Adafruit #"]
  SP1 = SPEAKER [package=pcb_mount_speaker]
  SP2 = SPEAKER [package=pcb_mount_speaker]
  Micro-switch = SPST Switch [package=switch-spdt-smd]

nets:
  3V3: RPI_4.3V3, Adafruit_Speaker_Bonnet.3.3V
  N1: RPI_4.5V, Adafruit_Speaker_Bonnet.5.0V
  GND: RPI_4.GND, Adafruit_Speaker_Bonnet.GND, Micro-switch.S
  N2: RPI_4.GPIO4, Micro-switch.P
  N3: RPI_4.GPIO18, Adafruit_Speaker_Bonnet.BCLK
  N4: RPI_4.GPIO19, Adafruit_Speaker_Bonnet.LRCLK
  N5: RPI_4.GPIO21, Adafruit_Speaker_Bonnet.DIN
  N6: Adafruit_Speaker_Bonnet.RIGHT-, SP1.+
  N7: Adafruit_Speaker_Bonnet.RIGHT+, SP1.-
  N8: Adafruit_Speaker_Bonnet.LEFT+, SP2.-
  N9: Adafruit_Speaker_Bonnet.LEFT-, SP2.+

custom parts:
  Adafruit Stereo 3W Speaker Bonnet: Hey Mr. DJ! Turn up that Raspberry Pi mix to the max with this cute 3W Stereo Amplifier Bonnet for Raspberry Pi. (It's not big enough to be an official HAT, so we called it a bonnet, you see?) It's the exact same size as a Raspberry Pi Zero but works with any and all Raspberry Pi computers with a 2x20 connector - A+, B+, Zero, Pi 2, Pi 3, etc. This Bonnet uses I2S a digital sound standard, so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
